# Fritzing sketch car_sketch (saved by Fritzing 1.0.5)
circuit board: 11.1455cm x 10.9907cm
breadboards: 1

parts:
  Arduino = Arduino Uno (Rev3) - ICSP
  M4 = gear-motor
  HC-SR04_Sensor_1 = HC-SR04 Ultrasonic Distance Sensor
  M3 = gear-motor
  S2 = H-Bridge with L298N
  Part1 = NRF24L01+ Breakout Board  # not connected
  VCC1 = 4 x AAA Battery Mount [internal_resistance=0.1Ω]

nets (from the breadboard view):
  N1: Arduino.A0, HC-SR04_Sensor_1.ECHO
  N2: Arduino.A1, HC-SR04_Sensor_1.TRIG
  GND: Arduino.GND, HC-SR04_Sensor_1.GND, S2.GND, VCC1.-
  N3: Arduino.D8, S2.IN3
  N4: Arduino.D2, S2.IN1
  N5: Arduino.D3_PWM, S2.ENA
  N6: Arduino.D4, S2.IN2
  N7: Arduino.D6_PWM, S2.ENB
  N8: Arduino.D7, S2.IN4
  VIN: Arduino.VIN, HC-SR04_Sensor_1.VCC, S2.5V
  N9: M4.pin_1, S2.M2-02
  N10: M4.pin_2, S2.M2-01
  N11: M3.pin_1, S2.M1-02
  N12: M3.pin_2, S2.M1-01
  N13: S2.12V, VCC1.+

custom parts:
  H-Bridge with L298N: h-bridge
